# Fritzing sketch Fritzing Sketch (saved by Fritzing 0.9.3b)
circuit board: 12.2202cm x 9.25688cm
breadboards: 1

parts:
  R3 = Resistor [tolerance=±5% resistance=220 package=THT]
  resetButton = Pushbutton [package="[THT]"]
  R4 = Resistor [tolerance=±5% resistance=220 package=THT]
  rightHandButton = Pushbutton [package="[THT]"]
  MELT_MT-16S2H-2FLA = LCD screen
  R5 = Resistor [tolerance=±5% resistance=220 package=THT]
  Part_1 = Arduino Uno (Rev3)
  R2 = Resistor [tolerance=±5% resistance=220 package=THT]
  R1 = Resistor [tolerance=±5% resistance=220 package=THT]
  GREEN_LED = LED - 5mm [color="Green (570nm)" package="5 mm [THT]"]
  leftHandButton = Pushbutton [package="[THT]"]
  RED_LED = LED - 5mm [color="Red (633nm)" package="5 mm [THT]"]

nets:
  N1: R3.Pin_0, Part_1.D4, leftHandButton.Pin_1, leftHandButton.Pin_2
  GND: R3.Pin_1, R4.Pin_1, MELT_MT-16S2H-2FLA.VSS, MELT_MT-16S2H-2FLA.V0, MELT_MT-16S2H-2FLA.R/W, MELT_MT-16S2H-2FLA.LED-, R5.Pin_1, Part_1.GND, GREEN_LED.cathode, RED_LED.cathode
  N2: resetButton.Pin_1, resetButton.Pin_2, R5.Pin_0, Part_1.D5_PWM
  5V: resetButton.Pin_3, resetButton.Pin_4, rightHandButton.Pin_3, rightHandButton.Pin_4, MELT_MT-16S2H-2FLA.VDD, MELT_MT-16S2H-2FLA.LED+, Part_1.5V, leftHandButton.Pin_3, leftHandButton.Pin_4
  N3: R4.Pin_0, rightHandButton.Pin_1, rightHandButton.Pin_2, Part_1.D3_PWM
  N4: MELT_MT-16S2H-2FLA.RS, Part_1.D8
  N5: MELT_MT-16S2H-2FLA.E, Part_1.D9_PWM
  N6: MELT_MT-16S2H-2FLA.DB4, Part_1.D10_PWM/SS
  N7: MELT_MT-16S2H-2FLA.DB5, Part_1.D11_PWM/MOSI
  N8: MELT_MT-16S2H-2FLA.DB6, Part_1.D12/MISO
  N9: MELT_MT-16S2H-2FLA.DB7, Part_1.D13/SCK
  N10: Part_1.D6_PWM, R1.Pin_0
  N11: Part_1.D7, R2.Pin_0
  N12: R2.Pin_1, GREEN_LED.anode
  N13: R1.Pin_1, RED_LED.anode

// code stored in the sketch: Fritzing Sketch.ino
#include <LiquidCrystal.h>
LiquidCrystal lcd(13, 12, 11, 10,  9,  8);
#define RED_LED 7
#define GREEN_LED 6
const int resetButton = 5;
const int leftHandButton = 4;
const int rightHandButton = 3;

int leftButtonState = 0;
int rightButtonState = 0;
int resetButtonState = 0;
int running = 0;
int count = 0;
unsigned long average = 0;
unsigned long oldTime = 0;

void(* resetFunc) (void) = 0;

void setup() {
  lcd.begin(16, 2);
  lcd.print("*SCTimerArduino*");
  pinMode (RED_LED, OUTPUT);
  pinMode (GREEN_LED, OUTPUT);
}
     
void loop() {
  lcd.setCursor(4,0);
  
  leftButtonState = digitalRead(leftHandButton);
  rightButtonState = digitalRead(rightHandButton);
  resetButtonState = digitalRead(resetButton);
  
  unsigned long currentTime = millis();
  unsigned long now = (currentTime - oldTime);
  unsigned long minutes = (now/1000)/60;
  unsigned long seconds = (now/1000)%60;
  unsigned long milliseconds = now%1000;
  
  // Reset timer
  if (resetButtonState) {
    resetFunc();
  }
  
  if (running) {
    print_time(minutes, seconds, milliseconds);
    digitalWrite(RED_LED, HIGH);
    delay(15);
    digitalWrite(GREEN_LED, LOW);
    delay(15);
    digitalWrite(RED_LED, LOW);
    delay(15);
    digitalWrite(GREEN_LED, HIGH);
  }
  
  // Start-Stop timer
  if (leftButtonState && rightButtonState) {
    if (running) {
      count += 1;
      average = (average+now)/count;
      stop_timer(minutes, seconds, milliseconds);
      print_average(average);
      running = 0;
    } else {
      while(leftButtonState && rightButtonState) {
          digitalWrite(RED_LED, HIGH);
          delay(500);
          leftButtonState = digitalRead(leftHandButton); 
          rightButtonState = digitalRead(rightHandButton);
          lcd.setCursor(0,0);
          lcd.print("     Ready?     ");
          lcd.setCursor(0,1);
          lcd.print("                 ");
          digitalWrite(GREEN_LED, HIGH);  
      }
      digitalWrite(RED_LED, LOW);
      digitalWrite(GREEN_LED, LOW);
      running = 1;
      unsigned long currentTime = millis();
      oldTime = currentTime;
    }
  }
}

void stop_timer(unsigned long minutes, unsigned long seconds, unsigned long milliseconds) {
  digitalWrite(RED_LED, LOW);
  digitalWrite(GREEN_LED, LOW);
  clear_lcd(minutes, seconds, milliseconds);
  delay(1000);
  unsigned long currentTime = millis();
  oldTime = currentTime;
}

void clear_lcd(unsigned long minutes, unsigned long seconds, unsigned long milliseconds) {
  lcd.clear();
  lcd.setCursor(0,0);
  lcd.print("ScTime:");
  lcd.setCursor(7,0);
  print_time(minutes, seconds, milliseconds);
}

void print_average(unsigned long average) {
  unsigned long minutes = (average/1000)/60;
  unsigned long seconds = (average/1000)%60;
  unsigned long milliseconds = average%1000;
  lcd.setCursor(0,1);
  char lcd_buffer[16];
  sprintf(lcd_buffer, "AvTime:%02lu:%02lu:%03lu", minutes, seconds, milliseconds);
  lcd.print(lcd_buffer);
}

void print_time(unsigned long minutes, unsigned long seconds, unsigned long milliseconds) {
  char lcd_buffer[9];
  sprintf(lcd_buffer, "%02lu:%02lu:%03lu", minutes, seconds, milliseconds);
  lcd.print(lcd_buffer);
}
